# Fritzing sketch fritzing (saved by Fritzing 0.8.7b)
breadboards: 2

parts:
  Componente1 = Arduino Ethernet Shield (Rev3)
  Componente2 = Arduino Due (Rev2b)
  R1 = Temperature Sensor (Thermistor) [thermistor_type=NTC package=THT]
  R8 = PHOTOCELL [package=photocell-kit]
  LED1 = LED - 3mm [color="Red (633nm)" package="3 mm [THT]"]
  LED2 = LED - 3mm [color="Green (555nm)" package="3 mm [THT]"]
  R11 = Resistor [tolerance=±5% resistance=1k package="1206 [SMD]"]
  R12 = Resistor [tolerance=±5% resistance=1k package="1206 [SMD]"]
  R13 = Resistor [tolerance=±5% resistance=1k package="1206 [SMD]"]
  R14 = Resistor [tolerance=±5% resistance=1k package="1206 [SMD]"]
  R15 = Resistor [tolerance=±5% resistance=1k package="1206 [SMD]"]
  R16 = Resistor [tolerance=±5% resistance=1k package="1206 [SMD]"]
  R17 = Resistor [tolerance=±5% resistance=1k package="1206 [SMD]"]
  R18 = Resistor [tolerance=±5% resistance=1k package="1206 [SMD]"]
  X = Basic Servo
  Y = Basic Servo
  BAT1 = BC9VPC [package=bc9vpc]
  Raspberry_Pi_rev1 = Raspberry Pi B rev2

nets:
  N1: Componente1.GND, R11.Pin_1, R12.Pin_0, R13.Pin_1, R14.Pin_0
  N2: Componente1.D8, Y.pulse
  N3: Componente1.D7, X.pulse
  N4: Componente1.RESET, Componente2.D40
  N5: Componente1.5V, R1.pin_0, R8.P$1
  N6: Componente2.A8, R1.pin_1, R18.Pin_1
  N7: Componente2.A10, R8.P$2, R13.Pin_0
  N8: Componente2.D52, LED2.anode
  N9: Componente2.D53, LED1.anode
  N10: LED1.cathode, R12.Pin_1
  N11: LED2.cathode, R11.Pin_0
  N12: R14.Pin_1, R15.Pin_0
  N13: R15.Pin_1, R16.Pin_0
  N14: R16.Pin_1, R17.Pin_0
  N15: R17.Pin_1, R18.Pin_0
  GND: X.gnd, Y.gnd, BAT1.V-, Raspberry_Pi_rev1.GND
  VCC: X.vcc, Y.vcc, BAT1.V+, Raspberry_Pi_rev1.5V
